# Fritzing sketch chave_optica (saved by Fritzing 0.8.7b)
circuit board: 2.72415cm x 2.61104cm
breadboards: 1

parts:
  R1 = Resistor [tolerance=±5% resistance=220 package=THT]
  R2 = Resistor [tolerance=±5% resistance=220 package=THT]
  U1 = AVR 10-pin ICSP Header [package="avr icsp"]
  J1 = female pin header, 3 pins [form="♀ (female)"]

nets:
  N1: R1.Pin_0, U1.2, J1.pin1
  N2: R1.Pin_1, R2.Pin_1, J1.pin3
  N3: R2.Pin_0, U1.9
  N4: U1.1, U1.3, U1.4, U1.5, U1.6, U1.7, U1.8, U1.10, J1.pin2
