# Fritzing sketch Diagrama_eletrico_carro (saved by Fritzing 0.8.7b)
breadboards: 1

parts:
  Arduino_Uno = Arduino Uno (Rev3)
  U6 = 2.4GHz Low Power Transceiver [package=qfn20]
  U7 = L298 [package=multiwatt15]
  M1 = DC Motor
  M2 = DC Motor
  Modulo_bluetooth = Bluetooth Mate Silver

nets:
  N1: Arduino_Uno.D8, U6.CE
  N2: Arduino_Uno.D11_PWM/MOSI, U6.MOSI
  N3: Arduino_Uno.D12/MISO, U6.MISO
  N4: Arduino_Uno.D13/SCK, U6.SCK
  GND: Arduino_Uno.GND, U6.VSS, U7.GND, Modulo_bluetooth.GND
  N5: Arduino_Uno.D0/RX, Modulo_bluetooth.TX_5V
  N6: Arduino_Uno.D1/TX, Modulo_bluetooth.RX_5V
  N7: Arduino_Uno.D2, U7.IN1
  N8: Arduino_Uno.D3_PWM, U7.IN2
  N9: Arduino_Uno.D4, U7.IN3
  N10: Arduino_Uno.D5_PWM, U7.IN4
  N11: Arduino_Uno.D7, U6.CSN
  3V3: Arduino_Uno.3V3, U6.VDD
  5V: Arduino_Uno.5V, Modulo_bluetooth.VCC
  9V: Arduino_Uno.VIN
  N12: U7.OUT1, M1.pin_1
  N13: U7.OUT2, M1.pin_2
  6V: U7.VS
  N14: U7.OUT3, M2.pin_1
  N15: U7.OUT4, M2.pin_2
